// Logisim project equal8.circ as structural Verilog: 1 circuit, main circuit main
module main (
  input  [7:0] m,
  input  [7:0] n,
  output m___n
);

  wire xnor_1_out, xnor_2_out, xnor_3_out, xnor_4_out, xnor_5_out, xnor_6_out, xnor_7_out, xnor_8_out;

  xnor xnor_1 (xnor_1_out, m[0], n[0]);
  xnor xnor_2 (xnor_2_out, m[1], n[1]);
  xnor xnor_3 (xnor_3_out, m[2], n[2]);
  xnor xnor_4 (xnor_4_out, m[3], n[3]);
  xnor xnor_5 (xnor_5_out, m[4], n[4]);
  xnor xnor_6 (xnor_6_out, m[5], n[5]);
  xnor xnor_7 (xnor_7_out, m[6], n[6]);
  xnor xnor_8 (xnor_8_out, m[7], n[7]);
  and and_1 (m___n, xnor_1_out, xnor_2_out, xnor_3_out, xnor_4_out, xnor_5_out, xnor_6_out, xnor_7_out, xnor_8_out);
endmodule
