// Logisim project inc8.circ as structural Verilog: 1 circuit, main circuit main
module main (
  input  [7:0] in_1,
  output [7:0] out_2
);

  wire and_1_out, and_2_out, and_3_out, and_4_out, and_5_out, and_6_out;

  and and_1 (and_1_out, in_1[5], and_6_out);
  and and_2 (and_2_out, in_1[6], and_1_out);
  xor xor_1 (out_2[0], 1'b1, in_1[0]);
  and and_3 (and_3_out, in_1[1], in_1[0]);
  and and_4 (and_4_out, in_1[2], and_3_out);
  and and_5 (and_5_out, in_1[3], and_4_out);
  and and_6 (and_6_out, in_1[4], and_5_out);
  xor xor_2 (out_2[1], in_1[0], in_1[1]);
  xor xor_3 (out_2[2], and_3_out, in_1[2]);
  xor xor_4 (out_2[3], and_4_out, in_1[3]);
  xor xor_5 (out_2[4], and_5_out, in_1[4]);
  xor xor_6 (out_2[5], and_6_out, in_1[5]);
  xor xor_7 (out_2[6], and_1_out, in_1[6]);
  xor xor_8 (out_2[7], and_2_out, in_1[7]);
endmodule
